# Fritzing sketch Radar_Sensor_Schematic (saved by Fritzing 1.0.6)

parts:
  A1 = Ai-thinker Rd-03D
  esp1 = ESP32 DevKitc V4

nets:
  N1: A1.Pin_1, A1.Pin_11, esp1.IO18
  N2: A1.Pin_2, A1.Pin_10, esp1.IO19
  N3: A1.Pin_3, A1.Pin_9, esp1.GND
  N4: A1.Pin_7, A1.Pin_8, esp1.5V

notes:
  GND
  5V
  RX
  TX
  TX
  RX

custom parts:
  Ai-thinker Rd-03D: Rd-03D is a radar module developed by Shenzhen Ai-Thinker Technology Co., LTD, which is equipped with the S5KM312CL chip. S5KM312CL is an integrated microcontroller millimeter wave sensor SoC based on FMCW radar transceiver technology.
  ESP32 DevKitc V4: ESP32-DevKitC board with ESP32-WROOM-32 module. ESP32-DevKitC V4 is a small-sized ESP32-based development board produced by Espressif. Most of the pins on the ESP module are broken out to the pin headers on the board. The pins D0, D1, D2, D3, CMD and CLK are used internally for communication between ESP32 and SPI flash memory. They are grouped on both sides near the USB connector. Avoid using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
